# Fritzing sketch heat-switch-esp (saved by Fritzing 0.9.3b)
breadboards: 1

parts:
  Part1 = Arduino Nano (Rev3.0)
  T1 = LM35 Temperature Sensor [package="TO92 [THT]"]
  KY-1 = Keyes Relay [package=THT]
  Socket_de_entrada = Power plug
  Socket_de_saida = Power plug
  HLK-PM1 = HLK-PM01
  U1 = ESP8266 WiFi Module [part_number=ESP8266]

nets:
  N1: Part1.D1/TX, U1.TXD
  N2: Part1.D0/RX, U1.RXD
  GND: Part1.GND, T1.GND, KY-1.ground, HLK-PM1.-Vo, U1.GND
  N3: Part1.D10, KY-1.signal
  N4: Part1.VIN, HLK-PM1.+Vo
  N5: Part1.5V, T1.+Vs, KY-1.power
  N6: Part1.A0, T1.Vout
  3V3: Part1.3V3, U1.VCC, U1.CH_PD
  N7: KY-1.C, Socket_de_entrada.VCC, HLK-PM1.AC#0
  N8: KY-1.NO, Socket_de_saida.VCC
  GND_2: Socket_de_entrada.GND, Socket_de_saida.GND, HLK-PM1.AC#1

notes:
  Este socket deverá ser ligado no equipamento a ser controlado
  Este socket deverá ser ligado na rede de energia

custom parts:
  Keyes Relay: The Keyes 5V relay module is suitable for SCM development, home appliance control. It uses a 5V~12V TIL control signal which can control DC / AC signal.
  ESP8266 WiFi Module: Generic WiFi Module based on the ESP8266 with onboard PCB antenna and UART communications
