# Fritzing sketch heat-switch-nrf (saved by Fritzing 0.9.3b)
breadboards: 1

parts:
  Part1 = Arduino Nano (Rev3.0)
  T1 = LM35 Temperature Sensor [package="TO92 [THT]"]
  KY-1 = Keyes Relay [package=THT]
  Socket_de_entrada = Power plug
  Socket_de_saida = Power plug
  HLK-PM1 = HLK-PM01
  NRF24L1 = NRF24L01
  Raspberry_Pi_B_rev1 = Raspberry Pi B rev1
  NRF24L2 = NRF24L01

nets:
  GND: Part1.GND, T1.GND, KY-1.ground, HLK-PM1.-Vo, NRF24L1.GND
  N1: Part1.D7, NRF24L1.CE
  N2: Part1.D8, NRF24L1.CSN
  N3: Part1.D10, KY-1.signal
  N4: Part1.D11/MOSI, NRF24L1.MOSI
  N5: Part1.D12/MISO, NRF24L1.MISO
  N6: Part1.VIN, HLK-PM1.+Vo
  N7: Part1.5V, T1.+Vs, KY-1.power
  N8: Part1.A0, T1.Vout
  3V3: Part1.3V3, NRF24L1.VCC
  N9: Part1.D13/SCK, NRF24L1.SCK
  N10: KY-1.C, Socket_de_entrada.VCC, HLK-PM1.AC#0
  N11: KY-1.NO, Socket_de_saida.VCC
  GND_2: Socket_de_entrada.GND, Socket_de_saida.GND, HLK-PM1.AC#1
  3V3_2: Raspberry_Pi_B_rev1.3V3, NRF24L2.VCC
  GND_3: Raspberry_Pi_B_rev1.GND, NRF24L2.GND
  N12: Raspberry_Pi_B_rev1.GPIO_10, NRF24L2.MOSI
  N13: Raspberry_Pi_B_rev1.GPIO_9, NRF24L2.MISO
  N14: Raspberry_Pi_B_rev1.GPIO_25, NRF24L2.CE
  N15: Raspberry_Pi_B_rev1.GPIO_11, NRF24L2.SCK
  N16: Raspberry_Pi_B_rev1.GPIO_8, NRF24L2.CSN

notes:
  Este socket deverá ser ligado no equipamento a ser controlado
  Este socket deverá ser ligado na rede de energia

custom parts:
  Keyes Relay: The Keyes 5V relay module is suitable for SCM development, home appliance control. It uses a 5V~12V TIL control signal which can control DC / AC signal.
  NRF24L01: NRF24L01 module
